// Digital circuit QPU.dig as structural Verilog
module QPU (
  input  [7:0] Input,
  input  Enable,
  output Write_RAM,
  output Write_I_O,
  output [7:0] RAM_Address,
  output Read_RAM,
  output Read_I_O,
  output [7:0] Output
);

  wire add_1_c_o, and_1_out, and_2_out, and_3_out, and_4_out, and_5_out, and_7_out, comparator_1_eq,
       comparator_1_lt, demultiplexer_1_out_0, demultiplexer_1_out_1, demultiplexer_2_out_0,
       demultiplexer_2_out_1, multiplexer_1_out, multiplexer_4_out, nor_1_out, or_1_out, State_nq, State_q,
       sub_1_c_o, undriven_3, Was_0_q, Was__lt_0_q, Was_Car_q;
  wire [2:0] Fetch_q, undriven_2;
  wire [7:0] A_q, add_1_s, B_q, counterpreset_1_out, sub_1_s;
  wire [7:3] undriven;

  T_FF State (.T(Enable), .C(undriven_3), .Q(State_q), .nQ(State_nq));
  Comparator comparator_1 (.a(Output[0]), .b(1'b0), .eq(comparator_1_eq), .lt(comparator_1_lt));  // open: gt
  and and_1 (and_1_out, State_q, undriven[3], undriven_3);
  D_FF Was_0 (.D(comparator_1_eq), .C(and_1_out), .Q(Was_0_q));  // open: nQ
  D_FF Was__lt_0 (.D(comparator_1_lt), .C(and_1_out), .Q(Was__lt_0_q));  // open: nQ
  D_FF Was_Car (.D(and_7_out), .C(and_1_out), .Q(Was_Car_q));  // open: nQ
  or or_1 (or_1_out, State_nq, and_5_out);
  Multiplexer #(.Selector_Bits(2)) multiplexer_1 (
    .sel(Fetch_q[1:0]), .in_0(1'b1), .in_1(Was_0_q), .in_2(Was__lt_0_q), .in_3(Was_Car_q),
    .out(multiplexer_1_out));
  Demultiplexer demultiplexer_1 (
    .sel(Fetch_q[2]), .in(State_q), .out_0(demultiplexer_1_out_0), .out_1(demultiplexer_1_out_1));
  and and_2 (and_2_out, multiplexer_1_out, demultiplexer_1_out_1);
  Demultiplexer #(.Selector_Bits(2)) demultiplexer_2 (
    .sel(Fetch_q[1:0]), .in(demultiplexer_1_out_0), .out_0(demultiplexer_2_out_0),
    .out_1(demultiplexer_2_out_1), .out_2(Write_RAM), .out_3(Write_I_O));
  and and_3 (and_3_out, Enable, or_1_out);
  CounterPreset #(.Bits(8)) counterpreset_1 (
    .en(and_3_out), .C(undriven_3), .dir(1'b0), .in(Output), .ld(and_2_out), .clr(1'b0),
    .out(counterpreset_1_out));  // open: ovf
  Register #(.Bits(8)) A (.D(Output), .C(undriven_3), .en(demultiplexer_2_out_0), .Q(A_q));
  Register #(.Bits(8)) B (.D(Output), .C(undriven_3), .en(demultiplexer_2_out_1), .Q(B_q));
  Register Fetch (.D(Input[0]), .C(undriven_3), .en(State_nq), .Q(Fetch_q[0]));
  Multiplexer #(.Bits(8)) multiplexer_2 (.sel(and_4_out), .in_0(counterpreset_1_out), .in_1(A_q), .out(RAM_Address));
  Add add_1 (.a(A_q[0]), .b(B_q[0]), .s(add_1_s[0]), .c_o(add_1_c_o));  // open: c_i
  Sub sub_1 (.a(A_q[0]), .b(B_q[0]), .s(sub_1_s[0]), .c_o(sub_1_c_o));  // open: c_i
  and and_4 (and_4_out, ~and_5_out, State_q);  // And
  Multiplexer #(.Selector_Bits(3), .Bits(8)) multiplexer_3 (
    .sel(undriven_2), .in_0(A_q), .in_1(Input), .in_2(add_1_s), .in_3(sub_1_s), .in_4(B_q),
    .in_5(counterpreset_1_out), .in_6(Input), .in_7(Input), .out(Output));
  and and_5 (and_5_out, undriven_2[0], undriven_2[1], undriven_2[2]);
  Multiplexer multiplexer_4 (.sel(undriven_2[0]), .in_0(add_1_c_o), .in_1(sub_1_c_o), .out(multiplexer_4_out));
  nor nor_1 (nor_1_out, undriven_2[2], undriven_2[1]);
  and and_6 (Read_I_O, undriven_2[2], undriven_2[1], ~undriven_2[0]);  // And
  and and_7 (and_7_out, ~undriven_2[2], undriven_2[1], multiplexer_4_out);  // And
  and and_8 (Read_RAM, nor_1_out, undriven_2[0]);
  // Pins of 1 and 8 bits meet at Output
  // Pins of 1 and 8 bits meet at A_q
  // Pins of 1 and 8 bits meet at B_q
  // Pins of 1 and 8 bits meet at Input
  // Pins of 1 and 8 bits meet at add_1_s
  // Pins of 1 and 8 bits meet at sub_1_s
  // Pins of 1 and 8 bits meet at {undriven[7], undriven_2, undriven[3], Fetch_q}

  // Notes on the sheet:
  //   Executing
  //   Set Flags
  //   Immediate
  //   Is Jump
  //   ~2 & 1 = A+B | A-B
  //   Then & w/ carry
endmodule
