// Digital circuit QPU.dig as structural Verilog
// A small, Super RISC CPU.
// Every instruction is a MOV instruction or a HLT instruction.
// See the QTL for how to use it.
module QPU (
  input  En,
  input  Clk,
  input  [7:0] In,
  input  IOR,
  output [7:0] MA,
  output [7:0] Out,
  output WM,
  output WP,
  output RM,
  output RP,
  output Hlt
);

  wire and_1_out, and_2_out, and_3_out, and_4_out, and_5_out, and_7_out, and_8_out, demultiplexer_1_out_0,
       demultiplexer_1_out_1, demultiplexer_2_out_0, demultiplexer_2_out_1, multiplexer_1_out, or_1_out,
       Out_CMP_eq, Out_CMP_lt, State_nq, State_q, Was_0_q, Was__lt_0_q;
  wire [2:0] driver_1_out, driver_1_out_3;
  wire [3:3] driver_1_out_2;
  wire [7:0] A_q, add_1_s, B_q, Fetch_q, PC_out, sub_1_s;

  T_FF State (.T(En), .C(Clk), .Q(State_q), .nQ(State_nq));
  Comparator #(.Signed("true"), .Bits(8)) Out_CMP (
    .a(Out), .b({8{1'b0}}), .eq(Out_CMP_eq), .lt(Out_CMP_lt));  // open: gt
  and and_1 (and_1_out, and_2_out, driver_1_out_2[3], Clk);
  Demultiplexer demultiplexer_1 (
    .sel(driver_1_out[2]), .in(and_2_out), .out_0(demultiplexer_1_out_0), .out_1(demultiplexer_1_out_1));
  and and_2 (and_2_out, En, State_q);
  and and_3 (and_3_out, En, State_nq);
  D_FF Was_0 (.D(Out_CMP_eq), .C(and_1_out), .Q(Was_0_q));  // open: nQ
  D_FF Was__lt_0 (.D(Out_CMP_lt), .C(and_1_out), .Q(Was__lt_0_q));  // open: nQ
  Register #(.Bits(8)) Fetch (.D(In), .C(Clk), .en(and_3_out), .Q(Fetch_q));
  Demultiplexer #(.Selector_Bits(2)) demultiplexer_2 (
    .sel(driver_1_out[1:0]), .in(demultiplexer_1_out_0), .out_0(demultiplexer_2_out_0),
    .out_1(demultiplexer_2_out_1), .out_2(WP), .out_3(WM));
  assign {Hlt, driver_1_out_3, driver_1_out_2[3], driver_1_out} = and_2_out ? Fetch_q : 8'bz;  // Driver driver_1
  Multiplexer #(.Selector_Bits(2)) multiplexer_1 (
    .sel(driver_1_out[1:0]), .in_0(1'b1), .in_1(Was_0_q), .in_2(Was__lt_0_q), .in_3(IOR),
    .out(multiplexer_1_out));
  Register #(.Bits(8)) A (.D(Out), .C(Clk), .en(demultiplexer_2_out_0), .Q(A_q));
  Register #(.Bits(8)) B (.D(Out), .C(Clk), .en(demultiplexer_2_out_1), .Q(B_q));
  PullDown #(.Bits(8)) pulldown_1 (.out({Hlt, driver_1_out_3, driver_1_out_2[3], driver_1_out}));
  or or_1 (or_1_out, and_3_out, and_7_out);
  and and_4 (and_4_out, multiplexer_1_out, demultiplexer_1_out_1);
  Add #(.Bits(8)) add_1 (.a(A_q), .b(B_q), .c_i(1'b0), .s(add_1_s));  // open: c_o
  Sub #(.Bits(8)) sub_1 (.a(A_q), .b(B_q), .c_i(1'b0), .s(sub_1_s));  // open: c_o
  CounterPreset #(.Bits(8), .isProgramCounter("true")) PC (
    .en(or_1_out), .C(Clk), .dir(1'b0), .in(Out), .ld(and_4_out), .clr(1'b0), .out(PC_out));  // open: ovf
  and and_5 (and_5_out, ~driver_1_out_3[2], driver_1_out_3[1], driver_1_out_3[0]);  // And
  and and_6 (RP, ~driver_1_out_3[2], driver_1_out_3[1], ~driver_1_out_3[0]);  // And
  and and_7 (and_7_out, driver_1_out_3[2], driver_1_out_3[1], driver_1_out_3[0]);
  Multiplexer #(.Bits(8)) multiplexer_2 (.sel(and_8_out), .in_0(PC_out), .in_1(A_q), .out(MA));
  Multiplexer #(.Selector_Bits(3), .Bits(8)) multiplexer_3 (
    .sel(driver_1_out_3), .in_0(A_q), .in_1(B_q), .in_2(In), .in_3(In), .in_4(PC_out), .in_5(add_1_s),
    .in_6(sub_1_s), .in_7(In), .out(Out));
  and and_8 (and_8_out, ~and_7_out, and_2_out);  // And
  or or_2 (RM, and_5_out, and_7_out, and_3_out);

  // Notes on the sheet:
  //   En: Enable the CPU.
  //    - CPU continues executing code while this pin is held high.
  //    - If the pin is low, the CPU will not do anything.
  //   MA: The current memory address output.
  //   Out: The general purpose CPU output.
  //    - This is shared between I/O and RAM.
  //   WM: The CPU is writing to memory.
  //   WP: The CPU is writing to the I/O port.
  //   RM: The CPU is reading from memory.
  //   RP: The CPU is reading from the I/O port.
  //   Clk: Clock input.
  //   In: The general purpose input for the CPU.
  //    - This input is shared between I/O and RAM.
  //   Hlt: The CPU wants to halt.
  //    - The CPU cannot halt on its own, this must be handled externally.
  //   IOR: Should be high if the I/O is reading the CPU's output.
  //   Executing
  //   Set Flags
  //   Is Jump
  //   Immediate
  //   Read [A]
  //   Read I/O
endmodule
