// Digital circuit A & B Controller.dig as structural Verilog
module A___B_Controller (
  input  [7:0] Data_Input,
  input  Clock,
  input  Write_A,
  input  SWP,
  input  SPC_A_Enable,
  input  [1:0] SPC_A_Select,
  input  Write_B,
  input  [1:0] SPC_B_Select,
  input  SPC_B_Enable,
  output [7:0] A,
  output [7:0] B
);

  wire or_1_out, or_2_out, or_3_out, or_4_out;
  wire [7:0] add_1_s, add_2_s, multiplexer_1_out, multiplexer_2_out, multiplexer_3_out, multiplexer_4_out,
       multiplexer_5_out, multiplexer_6_out, neg_1_out, neg_2_out, sub_1_s, sub_2_s;

  Neg #(.Bits(8)) neg_1 (.in(A), .out(neg_1_out));
  Add #(.Bits(8)) add_1 (.a(A), .b(8'h1), .c_i(1'b0), .s(add_1_s));  // open: c_o
  Sub #(.Bits(8)) sub_1 (.a(A), .b(8'h1), .c_i(1'b0), .s(sub_1_s));  // open: c_o
  Neg #(.Bits(8)) neg_2 (.in(B), .out(neg_2_out));
  Add #(.Bits(8)) add_2 (.a(B), .b(8'h1), .c_i(1'b0), .s(add_2_s));  // open: c_o
  Sub #(.Bits(8)) sub_2 (.a(B), .b(8'h1), .c_i(1'b0), .s(sub_2_s));  // open: c_o
  Multiplexer #(.Selector_Bits(2), .Bits(8)) multiplexer_1 (
    .sel(SPC_A_Select), .in_0({8{1'b0}}), .in_1(neg_1_out), .in_2(add_1_s), .in_3(sub_1_s),
    .out(multiplexer_1_out));
  Multiplexer #(.Selector_Bits(2), .Bits(8)) multiplexer_2 (
    .sel(SPC_B_Select), .in_0({8{1'b0}}), .in_1(neg_2_out), .in_2(add_2_s), .in_3(sub_2_s),
    .out(multiplexer_2_out));
  Multiplexer #(.Bits(8)) multiplexer_3 (.sel(SWP), .in_0(multiplexer_1_out), .in_1(B), .out(multiplexer_3_out));
  Multiplexer #(.Bits(8)) multiplexer_4 (.sel(SWP), .in_0(multiplexer_2_out), .in_1(A), .out(multiplexer_4_out));
  Multiplexer #(.Bits(8)) multiplexer_5 (
    .sel(or_1_out), .in_0(Data_Input), .in_1(multiplexer_3_out), .out(multiplexer_5_out));
  or or_1 (or_1_out, SPC_A_Enable, SWP);
  Multiplexer #(.Bits(8)) multiplexer_6 (
    .sel(or_2_out), .in_0(Data_Input), .in_1(multiplexer_4_out), .out(multiplexer_6_out));
  or or_2 (or_2_out, SPC_B_Enable, SWP);
  or or_3 (or_3_out, or_1_out, Write_A);
  or or_4 (or_4_out, or_2_out, Write_B);
  Register #(.Bits(8)) u_A (.D(multiplexer_5_out), .C(Clock), .en(or_3_out), .Q(A));
  Register #(.Bits(8)) u_B (.D(multiplexer_6_out), .C(Clock), .en(or_4_out), .Q(B));
endmodule
