// Digital circuit Addressing.dig as structural Verilog
module Addressing (
  input  State_1,
  input  State_0,
  input  Immediate,
  input  [7:0] A_B,
  input  [7:0] A_plus_B,
  input  [7:0] B_A,
  input  [1:0] SPC_Select,
  input  SPC_Flag,
  input  Write_Flags,
  input  IOR,
  input  [1:0] Jump_Condition,
  input  Jump,
  input  Clk,
  input  [7:0] Data_Input,
  input  [7:0] A,
  output [7:0] MA,
  output [7:0] PC
);

  wire and_1_out, and_2_out, and_3_out, multiplexer_3_out, or_1_out, Out_CMP_eq, Out_CMP_lt, Was_0_q,
       Was__lt_0_q;
  wire [7:0] multiplexer_1_out, multiplexer_2_out;

  Multiplexer #(.Selector_Bits(2), .Bits(8)) multiplexer_1 (
    .sel(SPC_Select), .in_0(8'h1), .in_1(A_B), .in_2(A_plus_B), .in_3(B_A), .out(multiplexer_1_out));
  Multiplexer #(.Bits(8)) multiplexer_2 (
    .sel(SPC_Flag), .in_0(Data_Input), .in_1(multiplexer_1_out), .out(multiplexer_2_out));
  Comparator #(.Signed("true"), .Bits(8)) Out_CMP (
    .a(multiplexer_2_out), .b({8{1'b0}}), .eq(Out_CMP_eq), .lt(Out_CMP_lt));  // open: gt
  and and_1 (and_1_out, State_1, Write_Flags, Clk);
  D_FF Was_0 (.D(Out_CMP_eq), .C(and_1_out), .Q(Was_0_q));  // open: nQ
  D_FF Was__lt_0 (.D(Out_CMP_lt), .C(and_1_out), .Q(Was__lt_0_q));  // open: nQ
  Multiplexer #(.Selector_Bits(2)) multiplexer_3 (
    .sel(Jump_Condition), .in_0(1'b1), .in_1(Was_0_q), .in_2(Was__lt_0_q), .in_3(IOR), .out(multiplexer_3_out));
  or or_1 (or_1_out, State_0, Immediate);
  and and_2 (and_2_out, multiplexer_3_out, Jump);
  CounterPreset #(.Bits(8), .isProgramCounter("true")) u_PC (
    .en(or_1_out), .C(Clk), .dir(1'b0), .in(Data_Input), .ld(and_2_out), .clr(1'b0), .out(PC));  // open: ovf
  Multiplexer #(.Bits(8)) multiplexer_4 (.sel(and_3_out), .in_0(PC), .in_1(A), .out(MA));
  and and_3 (and_3_out, ~Immediate, State_1);  // And
  // Pins of 1 and 8 bits meet at A
  // Pins of 1 and 2 bits meet at Jump_Condition

  // Notes on the sheet:
  //   Clk: Clock input.
endmodule
