// Digital circuit Control Unit.dig as structural Verilog
module Control_Unit (
  input  [7:0] Instruction_Input,
  input  Enable,
  input  Clock,
  output State_Execute__1,
  output State_Fetch__0,
  output [1:0] Jump_Condition,
  output Jump,
  output Write_A,
  output Write_B,
  output WP,
  output WM,
  output [2:0] Read_Select,
  output Write_Flags,
  output RM,
  output RP,
  output Immediate_Value,
  output [1:0] SPC_Select,
  output SPC_A,
  output SPC_B,
  output SPC_FLG,
  output SWP,
  output Hlt
);

  wire and_3_out, and_4_out, and_6_out, demultiplexer_1_out_0, not_1_out, State_nq, State_q;
  wire [3:2] driver_2_out;
  wire [7:0] Fetch_q;
  wire [7:2] driver_1_out;

  T_FF State (.T(Enable), .C(Clock), .Q(State_q), .nQ(State_nq));
  and and_1 (State_Execute__1, Enable, State_q);
  and and_2 (State_Fetch__0, Enable, State_nq);
  Register #(.Bits(8)) Fetch (.D(Instruction_Input), .C(Clock), .en(State_Fetch__0), .Q(Fetch_q));
  assign {driver_1_out, SPC_Select} = State_Execute__1 ? Fetch_q : 8'bz;  // Driver driver_1
  PullDown #(.Bits(8)) pulldown_1 (.out({driver_1_out, SPC_Select}));
  assign {Read_Select, driver_2_out, Jump_Condition} = not_1_out ? {driver_1_out[6:2], SPC_Select} : 7'bz;  // Driver driver_2
  not not_1 (not_1_out, driver_1_out[7]);
  and and_3 (and_3_out, ~driver_1_out[7], State_Execute__1);  // And
  PullDown #(.Bits(7)) pulldown_2 (.out({Read_Select, driver_2_out, Jump_Condition}));
  and and_4 (and_4_out, driver_1_out[6], driver_1_out[7]);
  and and_5 (Hlt, ~driver_1_out[6], driver_1_out[7]);  // And
  Demultiplexer demultiplexer_1 (.sel(driver_2_out[2]), .in(and_3_out), .out_0(demultiplexer_1_out_0), .out_1(Jump));
  Demultiplexer #(.Selector_Bits(2)) demultiplexer_2 (
    .sel(driver_1_out[3:2]), .in(and_4_out), .out_0(SPC_A), .out_1(SPC_B), .out_2(SPC_FLG), .out_3(SWP));
  Demultiplexer #(.Selector_Bits(2)) demultiplexer_3 (
    .sel(Jump_Condition), .in(demultiplexer_1_out_0), .out_0(Write_A), .out_1(Write_B), .out_2(WP), .out_3(WM));
  or or_1 (Write_Flags, driver_2_out[3], SPC_FLG);
  and and_6 (and_6_out, ~Read_Select[2], Read_Select[1], Read_Select[0]);  // And
  and and_7 (RP, ~Read_Select[2], Read_Select[1], ~Read_Select[0]);  // And
  and and_8 (Immediate_Value, Read_Select[2], Read_Select[1], Read_Select[0]);
  or or_2 (RM, and_6_out, Immediate_Value, State_Fetch__0);

  // Notes on the sheet:
  //   State Machine
  //   Execution Controls
  //   Special Decoding (QPUX)
  //   Write Decoding
  //   Main Decoding
endmodule
