// Digital circuit QPUX.dig as structural Verilog
// A small, Super RISC CPU.
// Every instruction is a MOV instruction or a HLT instruction.
// See the QTL for how to use it.
module QPUX (
  input  En,
  input  Clk,
  input  [7:0] In,
  input  IOR,
  output [7:0] MA,
  output [7:0] Out,
  output WM,
  output WP,
  output RM,
  output RP,
  output Hlt
);

  wire addressing_1_p8, control_unit_1_p4, control_unit_1_p5, control_unit_1_p6, control_unit_1_p7,
       control_unit_1_p8, control_unit_1_p9, control_unit_1_p13, control_unit_1_p16, control_unit_1_p18,
       control_unit_1_p19, undriven;
  wire [1:0] control_unit_1_p17;
  wire [2:0] control_unit_1_p12;
  wire [7:0] a___b_controller_1_a, a___b_controller_1_b, addressing_1_p4, addressing_1_p5, addressing_1_p6,
       addressing_1_p17;

  // Control_Unit control_unit_1: pin names not known; wires that end beside it: In, En, Clk, control_unit_1_p4, control_unit_1_p5, control_unit_1_p6, control_unit_1_p7, control_unit_1_p8, control_unit_1_p9, WP, WM, control_unit_1_p12, control_unit_1_p13, RM, RP, control_unit_1_p16, control_unit_1_p17, control_unit_1_p18, control_unit_1_p19
  A___B_Controller a___b_controller_1 (
    .Data_Input(Out), .Clock(Clk), .Write_A(control_unit_1_p8), .SWP(undriven),
    .SPC_A_Enable(control_unit_1_p18), .SPC_A_Select(control_unit_1_p17), .Write_B(control_unit_1_p9),
    .SPC_B_Select(control_unit_1_p17), .SPC_B_Enable(control_unit_1_p19), .A(a___b_controller_1_a),
    .B(a___b_controller_1_b));
  // Addressing addressing_1: pin names not known; wires that end beside it: control_unit_1_p4, control_unit_1_p5, control_unit_1_p16, addressing_1_p4, addressing_1_p5, addressing_1_p6, control_unit_1_p17, addressing_1_p8, control_unit_1_p13, IOR, control_unit_1_p6, control_unit_1_p7, Clk, Out, a___b_controller_1_a, MA, addressing_1_p17
  Add #(.Bits(8)) add_1 (
    .a(a___b_controller_1_a), .b(a___b_controller_1_b), .c_i(1'b0), .s(addressing_1_p5));  // open: c_o
  Sub #(.Bits(8)) sub_1 (
    .a(a___b_controller_1_a), .b(a___b_controller_1_b), .c_i(1'b0), .s(addressing_1_p4));  // open: c_o
  Sub #(.Bits(8)) sub_2 (
    .a(a___b_controller_1_b), .b(a___b_controller_1_a), .c_i(1'b0), .s(addressing_1_p6));  // open: c_o
  Multiplexer #(.Bits(8), .Selector_Bits(3)) multiplexer_1 (
    .sel(control_unit_1_p12), .in_0(a___b_controller_1_a), .in_1(a___b_controller_1_b), .in_2(In), .in_3(In),
    .in_4(addressing_1_p17), .in_5(addressing_1_p5), .in_6(addressing_1_p4), .in_7(In), .out(Out));

  // Notes on the sheet:
  //   En: Enable the CPU.
  //    - CPU continues executing code while this pin is held high.
  //    - If the pin is low, the CPU will not do anything.
  //   MA: The current memory address output.
  //   Out: The general purpose CPU output.
  //    - This is shared between I/O and RAM.
  //   WM: The CPU is writing to memory.
  //   WP: The CPU is writing to the I/O port.
  //   RM: The CPU is reading from memory.
  //   RP: The CPU is reading from the I/O port.
  //   Clk: Clock input.
  //   In: The general purpose input for the CPU.
  //    - This input is shared between I/O and RAM.
  //   Hlt: The CPU wants to halt.
  //    - The CPU cannot halt on its own, this must be handled externally.
  //   IOR: Should be high if the I/O is reading the CPU's output.
endmodule
