// Digital circuit Interface Q1.dig as structural Verilog
// A small, Super RISC CPU.
// Every instruction is a MOV instruction or a HLT instruction.
// See the QTL for how to use it.
module Interface_Q1 (
  input  Clk_In,
  input  Send,
  input  Read,
  input  [7:0] User_In,
  input  [7:0] Comp_In,
  input  RP,
  input  WP,
  output [7:0] User_Out,
  output Writing,
  output [7:0] Comp_Out,
  output Reading
);

  wire rs_ff_as_1_q, rs_ff_as_2_q;
  wire [7:0] d_ff_1_q;

  RS_FF_AS rs_ff_as_1 (.S(Send), .R(Writing), .Q(rs_ff_as_1_q));  // open: nQ
  D_FF #(.Bits(8)) d_ff_1 (.D(User_In), .C(Send), .Q(d_ff_1_q));  // open: nQ
  RS_FF_AS rs_ff_as_2 (.S(Read), .R(Reading), .Q(rs_ff_as_2_q));  // open: nQ
  RS_FF rs_ff_1 (.S(rs_ff_as_1_q), .C(Clk_In), .R(RP), .Q(Writing));  // open: nQ
  Register #(.Bits(8)) register_1 (.D(d_ff_1_q), .C(Clk_In), .en(rs_ff_as_1_q), .Q(Comp_Out));
  RS_FF rs_ff_2 (.S(rs_ff_as_2_q), .C(Clk_In), .R(WP), .Q(Reading));  // open: nQ
  Register #(.Bits(8)) register_2 (.D(Comp_In), .C(Clk_In), .en(WP), .Q(User_Out));

  // Notes on the sheet:
  //   Clk_In: Used to synchronize the interface.
  //   Send: Send the input data to the computer.
  //   Read: Turn on to mark user output as read.
  //   User_In: The data to send to the computer.
  //   User_Out: Data output for the user to read.
  //   Writing: On if writing to the computer (connect to IOW)
  //   Comp_In: The data coming from the computer (connect to Out)
  //   RP: Turn on if computer is reading from the interface.
  //   Comp_Out: Output TO the computer (connect to In)
  //   WP: Turn on if computer is writing to interface.
  //   Reading: On if reading from the computer (connect to IOR)
endmodule
