// Digital circuit QTC.dig as structural Verilog
// A simple computer which implements the QPU processor.
// It handles the enable and halt pins for the user.
// It handles switching between RAM and I/O.
// It also implements a simple read-from-input protocol which allows the use of an IOW pin in addition to the CPU's IOR pin.
// Note: The computer contains program memory!
module QTC (
  input  S_P,
  input  Clk,
  input  IOW,
  input  [7:0] In,
  input  IOR,
  output Running,
  output [7:0] Out,
  output RP,
  output WP
);

  wire and_1_out, and_2_out, delay_1_out, delay_2_out, or_1_out, qpux_1_hlt, qpux_1_rm, qpux_1_rp, qpux_1_wm,
       rs_ff_1_q, t_ff_1_nq, t_ff_1_q;
  wire [7:0] driver_1_out, multiplexer_1_out, qpux_1_ma, qpux_1_out;

  RS_FF rs_ff_1 (.S(IOW), .C(~qpux_1_rp), .R(rs_ff_1_q), .Q(rs_ff_1_q));  // open: nQ
  Delay delay_1 (.in(S_P), .out(delay_1_out));
  Delay delay_2 (.in(qpux_1_hlt), .out(delay_2_out));
  Multiplexer #(.Bits(8)) multiplexer_1 (.sel(rs_ff_1_q), .in_0({{7{1'b0}}, IOW}), .in_1(In), .out(multiplexer_1_out));
  and and_1 (and_1_out, S_P, ~delay_1_out);  // And
  and and_2 (and_2_out, qpux_1_hlt, ~delay_2_out);  // And
  assign driver_1_out = qpux_1_rp ? multiplexer_1_out : 8'bz;  // Driver driver_1
  or or_1 (or_1_out, and_1_out, and_2_out);
  QPUX qpux_1 (
    .En(Running), .Clk(Clk), .In(driver_1_out), .IOR(IOR), .MA(qpux_1_ma), .Out(qpux_1_out), .WM(qpux_1_wm),
    .WP(WP), .RM(qpux_1_rm), .RP(qpux_1_rp), .Hlt(qpux_1_hlt));
  T_FF t_ff_1 (.T(1'b1), .C(or_1_out), .Q(t_ff_1_q), .nQ(t_ff_1_nq));
  RS_FF u_Running (.S(t_ff_1_q), .C(Clk), .R(t_ff_1_nq), .Q(Running));  // open: nQ
  and and_3 (RP, qpux_1_rp, rs_ff_1_q);
  RAMDualPort #(.AddrBits(8), .isProgramMemory("true"), .Bits(8)) Program_Memory (
    .A(qpux_1_ma), .Din(qpux_1_out), .str(qpux_1_wm), .C(Clk), .ld(qpux_1_rm), .D(driver_1_out));
  assign Out = WP ? qpux_1_out : 8'bz;  // Driver driver_2

  // Notes on the sheet:
  //   Running: High if the computer is running.
  //   S_P: Start if not running, or pause if running.
  //   Clk: The computer & CPU clock.
  //   Out: The data output portion of the I/O.
  //   RP: On if the computer is reading the I/O port
  //   IOW: Should be high if the I/O is writing to the computer.
  //   WP: On if the computer is writing to the I/O port.
  //   In: The data input portion of the I/O.
  //   IOR: Should be high if the I/O is reading from the computer.
  //   I/O writing logic
  //   Computer start/stop logic
endmodule
