// Digital circuit QT Sandbox.dig as structural Verilog
module QT_Sandbox (
  input  clk,
  input  [7:0] Input
);

  wire qpc_1_rp, qpc_1_running, qpc_1_wp, rs_ff_1_q, rs_ff_as_1_q, Send_out, Turn_On_out;
  wire [7:0] d_ff_1_q, Out_q, qpc_1_out, register_1_q;

  Button Turn_On (.out(Turn_On_out));
  Button Send (.out(Send_out));
  RS_FF_AS rs_ff_as_1 (.S(Send_out), .R(rs_ff_1_q), .Q(rs_ff_as_1_q));  // open: nQ
  D_FF #(.Bits(8)) d_ff_1 (.D(Input), .C(Send_out), .Q(d_ff_1_q));  // open: nQ
  RS_FF rs_ff_1 (.S(rs_ff_as_1_q), .C(clk), .R(qpc_1_rp), .Q(rs_ff_1_q));  // open: nQ
  Register #(.Bits(8)) register_1 (.D(d_ff_1_q), .C(clk), .en(rs_ff_as_1_q), .Q(register_1_q));
  QPC qpc_1 (
    .S_P(Turn_On_out), .Clk(clk), .IOW(rs_ff_1_q), .In(register_1_q), .IOR(1'b1), .WP(qpc_1_wp),
    .Out(qpc_1_out), .RP(qpc_1_rp), .Running(qpc_1_running));
  LED led_1 (.in(qpc_1_running));
  Register #(.Bits(8)) Out (.D(qpc_1_out), .C(clk), .en(qpc_1_wp), .Q(Out_q));
  // Probe Output on Out_q

  // Notes on the sheet:
  //   clk: Hz: 8
endmodule
